# Fritzing sketch final_1 (saved by Fritzing 0.9.3b)
breadboards: 1

parts:
  R1 = Resistor [tolerance=±5% resistance=1k package=THT]
  R2 = Resistor [tolerance=±5% resistance=10k package=THT]
  DHT1 = DHT11 Humitidy and Temperature Sensor
  U1 = ESP8266 WiFi Module [part_number=ESP8266]
  Part1 = Arduino Uno (Rev3)

nets:
  N1: R1.Pin_0, R2.Pin_0, U1.RXD, U1.CH_PD, Part1.D2
  N2: R1.Pin_1, U1.TXD, Part1.D3_PWM
  VCC: R2.Pin_1, U1.VCC, Part1.3V3
  VDD: DHT1.VDD, Part1.5V
  N3: DHT1.DATA, Part1.D10_PWM/SS
  GND: DHT1.GND, U1.GND, Part1.GND

custom parts:
  DHT11 Humitidy and Temperature Sensor: DHT11 Humidity and Temperature Sensor
  ESP8266 WiFi Module: Generic WiFi Module based on the ESP8266 with onboard PCB antenna and UART communications
